// Digital circuit TwoBitBinaryMultiplier.dig as structural Verilog
module TwoBitBinaryMultiplier (
  input  [1:0] A,
  input  [1:0] B,
  output P3,
  output P2,
  output P1,
  output P0,
  output [3:0] Number_Output
);

  wire and_1_out, and_2_out, and_3_out, not_1_out, not_2_out, or_1_out;

  and and_1 (and_1_out, A[1], B[1]);
  and and_2 (and_2_out, A[1], B[0]);
  and and_3 (and_3_out, B[1], A[0]);
  and and_4 (Number_Output[0], B[0], A[0]);
  not not_1 (not_1_out, A[0]);
  or or_1 (or_1_out, not_1_out, not_2_out);
  not not_2 (not_2_out, B[0]);
  xor xor_1 (Number_Output[1], and_2_out, and_3_out);
  and and_5 (Number_Output[3], Number_Output[0], and_1_out);
  and and_6 (Number_Output[2], and_1_out, or_1_out);

  assign P0 = Number_Output[0];
  assign P1 = Number_Output[1];
  assign P2 = Number_Output[2];
  assign P3 = Number_Output[3];

  // Notes on the sheet:
  //   X
  //   A0
  //   A1
  //   B0
  //   B1
  //   A1B1
  //   A1B0
  //   A0B1
  //   A0B0
endmodule
